# Fritzing sketch 4dof_robotic_arm (saved by Fritzing 1.0.5)
breadboards: 1

parts:
  BATT1 = 3xAAA Switchable Battery Pack w/JST connector
  Part1 = Arduino Uno (Rev3)
  Part2 = Adafruit Analog 2-Axis Joystick [part_number="Adafruit #512"]
  Part3 = Adafruit Analog 2-Axis Joystick [part_number="Adafruit #512"]
  J2 = Basic Servo
  J3 = Basic Servo
  J4 = Basic Servo
  J5 = Basic Servo

nets:
  N1: BATT1.POS, Part1.VIN
  N2: Part1.A0, Part2.XOUT
  N3: Part1.A1, Part2.YOUT
  N4: Part1.A2, Part3.XOUT
  N5: Part1.A3, Part3.YOUT
  N6: Part1.D9_PWM, J5.pulse
  GND: Part1.GND, Part2.GND, J2.gnd, J3.gnd, J4.gnd, J5.gnd
  N7: Part1.D3_PWM, J3.pulse
  N8: Part1.D5_PWM, J2.pulse
  N9: Part1.D6_PWM, J4.pulse
  5V: Part1.5V, Part2.VCC
  VCC: J2.vcc, J3.vcc, J4.vcc, J5.vcc

custom parts:
  3xAAA Switchable Battery Pack w/JST connector: 3xAAA Switchable Battery Pack with JST connector
  Adafruit Analog 2-Axis Joystick: This mini-kit makes it easy to mount a PSP/Xbox-like thumb joystick to your project. The thumbstick is an analog joystick - more accurate and sensitive than just 'directional' joysticks - with a 'press in to select' button. Since it's analog, you'll need two analog reading pins on your microcontroller to determine X and Y. Having an extra digital input will let you read the switch. The pack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
