# Fritzing sketch diagram (saved by Fritzing 1.0.5)

parts:
  M1 = fc-51 [package=THT]
  M2 = fc-51 [package=THT]
  M3 = gear-motor
  M4 = gear-motor
  Part1 = Arduino Uno (Rev3)
  S1 = H-Bridge with L298N
  BATT1 = 3xAAA Switchable Battery Pack w/JST connector

nets:
  N1: M1.pin1, Part1.A0
  N2: M1.pin2, Part1.GND
  N3: M2.pin1, Part1.A1
  N4: M3.pin_1, S1.M2-01
  N5: M3.pin_2, S1.M2-02
  N6: M4.pin_1, S1.M1-01
  N7: M4.pin_2, S1.M1-02
  N8: Part1.D9_PWM, S1.IN4
  N9: Part1.D10_PWM/SS, S1.IN3
  N10: Part1.D11_PWM/MOSI, S1.IN1
  N11: Part1.D3_PWM, S1.ENB
  N12: Part1.D5_PWM, S1.ENA
  N13: Part1.D6_PWM, S1.IN2
  5V: Part1.5V, S1.5V
  N14: S1.12V, BATT1.POS
  N15: S1.GND, BATT1.NEG

custom parts:
  H-Bridge with L298N: h-bridge
  3xAAA Switchable Battery Pack w/JST connector: 3xAAA Switchable Battery Pack with JST connector
