# Fritzing sketch ir_car_diagram (saved by Fritzing 1.0.5)
breadboards: 1

parts:
  M1 = gear-motor
  M2 = gear-motor
  M3 = gear-motor
  M4 = gear-motor
  S1 = H-Bridge with L298N
  S2 = H-Bridge with L298N
  IR1 = TSOP312.., 314.. [package=THT]
  Part1 = Arduino Uno (Rev3)
  BATT1 = 3xAAA Switchable Battery Pack w/JST connector

nets:
  N1: M1.pin_1, S1.M2-02
  N2: M2.pin_1, S1.M1-02
  N3: M3.pin_2, S2.M1-01
  N4: M4.pin_1, S2.M2-02
  N5: S1.12V, BATT1.POS
  N6: S1.GND, BATT1.NEG
  5V: S1.5V, S2.5V, IR1.Vs, Part1.5V
  N7: S1.IN1, Part1.D3_PWM
  N8: S1.IN2, Part1.D4
  N9: S1.IN3, Part1.D5_PWM
  N10: S1.IN4, Part1.D6_PWM
  N11: S2.IN1, Part1.D7
  N12: S2.IN2, Part1.D8
  N13: S2.IN3, Part1.D9_PWM
  N14: S2.IN4, Part1.D10_PWM/SS
  GND: IR1.GND, Part1.GND
  N15: IR1.Data, Part1.D2

notes:
  Left Front
  Left Back
  Right Back
  Right Front

custom parts:
  H-Bridge with L298N: h-bridge
  3xAAA Switchable Battery Pack w/JST connector: 3xAAA Switchable Battery Pack with JST connector
