# Fritzing sketch diagram_file (saved by Fritzing 1.0.5)

parts:
  BATT1 = 3xAAA Switchable Battery Pack w/JST connector
  Part1 = Arduino Uno (Rev3)
  HC-SR04_Sensor_1 = HC-SR04 Ultrasonic Distance Sensor
  M1 = Dagu DGServo 9g (Pan and tilt) [part_number=RS001B]
  M2 = gear-motor
  M3 = gear-motor
  S1 = H-Bridge with L298N

nets:
  N1: BATT1.POS, S1.12V
  N2: BATT1.NEG, S1.GND
  N3: Part1.D9_PWM, S1.IN2
  N4: Part1.D10_PWM/SS, S1.IN3
  N5: Part1.D11_PWM/MOSI, S1.IN4
  N6: Part1.D12/MISO, HC-SR04_Sensor_1.TRIG
  N7: Part1.D13/SCK, HC-SR04_Sensor_1.ECHO
  GND: Part1.GND, HC-SR04_Sensor_1.GND, M1.gnd
  N8: Part1.D2, M1.pulse
  N9: Part1.D3_PWM, S1.ENA
  N10: Part1.D5_PWM, S1.ENB
  N11: Part1.D6_PWM, S1.IN1
  VCC: Part1.5V, HC-SR04_Sensor_1.VCC, M1.vcc
  N12: M2.pin_1, S1.M1-02
  N13: M2.pin_2, S1.M1-01
  N14: M3.pin_1, S1.M2-01
  N15: M3.pin_2, S1.M2-02

notes:
  Right
  Left

custom parts:
  3xAAA Switchable Battery Pack w/JST connector: 3xAAA Switchable Battery Pack with JST connector
  H-Bridge with L298N: h-bridge
