# Fritzing sketch smart_parking_system (saved by Fritzing 1.0.5)

parts:
  M1 = Dagu DGServo 9g (Top view) [part_number=RS001B]
  Part1 = Arduino Uno (Rev3) - ICSP
  M2 = fc-51 [package=THT]
  M3 = fc-51 [package=THT]
  M4 = fc-51 [package=THT]
  M5 = fc-51 [package=THT]
  M6 = fc-51 [package=THT]
  LCD2004-I2C1 = LCD2004-I2C

nets:
  GND: M1.gnd, Part1.GND, M4.pin2, M5.pin2, M6.pin2, LCD2004-I2C1.GND
  VCC: M1.vcc, Part1.5V, M4.pin3, M5.pin3, M6.pin3, LCD2004-I2C1.VCC
  N1: M1.pulse, Part1.D3_PWM
  N2: Part1.A4/SDA, LCD2004-I2C1.SDA
  N3: Part1.A5/SCL, LCD2004-I2C1.SCL
  N4: Part1.D2, M3.pin1
  N5: Part1.D4, M2.pin1
  N6: Part1.D5_PWM, M4.pin1
  N7: Part1.D6_PWM, M5.pin1
  N8: Part1.D7, M6.pin1

custom parts:
  LCD2004-I2C: A standard character display with 4x20 characters. Comes in many colors with LCM2004 IIC attached.
