# Fritzing sketch smart_waste_management_system (saved by Fritzing 1.0.5)

parts:
  Water_Level_Sensor1 = Water Level Sensor
  Part1 = Arduino Uno (Rev3) - ICSP
  M1 = Dagu DGServo 9g (Top view) [part_number=RS001B]
  HC-SR04_Sensor_1 = HC-SR04 Ultrasonic Distance Sensor
  BATT1 = 3xAAA Switchable Battery Pack w/JST connector

nets:
  N1: Water_Level_Sensor1.SIG, Part1.A0
  VCC: Water_Level_Sensor1.VCC, Part1.5V, M1.vcc, HC-SR04_Sensor_1.VCC
  GND: Water_Level_Sensor1.GND, Part1.GND, M1.gnd, BATT1.NEG
  N2: Part1.D8, M1.pulse
  N3: Part1.D9_PWM, HC-SR04_Sensor_1.ECHO
  N4: Part1.D10_PWM/SS, HC-SR04_Sensor_1.TRIG
  N5: Part1.VIN, BATT1.POS

custom parts:
  Water Level Sensor: A water level sensor. This sensor operates at 3V to 5V. The Sig (signal) pin outputs an analogue signal that is in proportion to the amount of water in contact with the sensor.
  3xAAA Switchable Battery Pack w/JST connector: 3xAAA Switchable Battery Pack with JST connector
